# Fritzing sketch ikeanametagsketch (saved by Fritzing 0.9.2b)
breadboards: 1

parts:
  Onderdeel1 = Arduino Uno (Rev3)
  LED1 = LED - 5mm [color="Red (633nm)" package="5 mm [THT]"]
  S1 = Pushbutton [package="[THT]"]
  R1 = Resistor [tolerance=±5% resistance=10k package=THT]

nets:
  N1: Onderdeel1.D13/SCK, LED1.anode
  N2: Onderdeel1.GND, LED1.cathode, S1.Pin_1, S1.Pin_2
  N3: Onderdeel1.D2, S1.Pin_3, S1.Pin_4, R1.Pin_0
  N4: Onderdeel1.5V, R1.Pin_1
